// Logisim project BCD to 7 segment display decoder.circ as structural Verilog: 1 circuit, main circuit main
module main (
  input  D,
  input  C,
  input  B,
  input  A
);

  wire and_1_out, and_2_out, and_3_out, and_4_out, and_5_out, and_6_out, and_7_out, and_8_out, and_9_out,
       and_10_out, and_11_out, and_12_out, and_13_out, and_14_out, and_15_out, and_16_out, not_1_out,
       not_2_out, not_3_out, not_4_out, not_5_out, not_6_out, not_7_out, not_8_out, not_9_out, not_10_out,
       not_11_out, not_12_out, not_13_out, not_14_out, not_15_out, not_16_out, not_17_out, not_18_out,
       not_19_out, not_20_out, not_21_out, or_1_out, or_2_out, or_3_out, or_4_out, or_5_out, or_6_out,
       or_7_out;

  not not_1 (not_1_out, C);
  not not_2 (not_2_out, A);
  not not_3 (not_3_out, B);
  not not_4 (not_4_out, A);
  not not_5 (not_5_out, B);
  not not_6 (not_6_out, C);
  not not_7 (not_7_out, A);
  not not_8 (not_8_out, C);
  not not_9 (not_9_out, A);
  not not_10 (not_10_out, B);
  not not_11 (not_11_out, C);
  not not_12 (not_12_out, A);
  not not_13 (not_13_out, A);
  not not_14 (not_14_out, B);
  not not_15 (not_15_out, A);
  not not_16 (not_16_out, B);
  not not_17 (not_17_out, A);
  not not_18 (not_18_out, C);
  not not_19 (not_19_out, B);
  not not_20 (not_20_out, A);
  and and_1 (and_1_out, not_1_out, not_2_out);
  and and_2 (and_2_out, C, A);
  not not_21 (not_21_out, C);
  and and_3 (and_3_out, not_3_out, not_4_out);
  and and_4 (and_4_out, B, A);
  or or_1 (or_1_out, not_5_out, A, C);
  and and_5 (and_5_out, not_6_out, not_7_out);
  and and_6 (and_6_out, not_8_out, B);
  and and_7 (and_7_out, B, not_9_out);
  and and_8 (and_8_out, C, not_10_out, A);
  and and_9 (and_9_out, not_11_out, not_12_out);
  and and_10 (and_10_out, B, not_13_out);
  and and_11 (and_11_out, not_14_out, not_15_out);
  and and_12 (and_12_out, C, not_16_out);
  and and_13 (and_13_out, C, not_17_out);
  and and_14 (and_14_out, not_18_out, B);
  and and_15 (and_15_out, C, not_19_out);
  and and_16 (and_16_out, C, not_20_out);
  or or_2 (or_2_out, and_1_out, B, and_2_out, D);
  or or_3 (or_3_out, not_21_out, and_3_out, and_4_out);
  or or_4 (or_4_out, and_5_out, and_6_out, and_7_out, and_8_out, D);
  or or_5 (or_5_out, and_9_out, and_10_out);
  or or_6 (or_6_out, and_11_out, and_12_out, and_13_out, D);
  or or_7 (or_7_out, and_14_out, and_15_out, and_16_out, D);
  _7_Segment_Display u_7_segment_display_1 (
    .g(or_7_out), .f(or_6_out), .a(or_2_out), .b(or_3_out), .e(or_5_out), .d(or_4_out), .c(or_1_out));  // open: dp

  // Notes on the sheet:
  //   c
  //   a
  //   b
  //   d
  //   e
  //   f
  //   g
  //   g
  //   a
  //   f
  //   b
  //   e
  //   d
  //   c
endmodule
