// Logisim project D to JK flip flop converter.circ as structural Verilog: 1 circuit, main circuit main
module main (
  input  J,
  input  K,
  output Q,
  output Q_prime
);

  wire and_1_out, and_2_out, clock_1_out, nand_1_out, nand_2_out, nand_3_out, nand_4_out, nand_5_out,
       nand_6_out, not_1_out, not_2_out, or_1_out;

  and and_1 (and_1_out, Q_prime, J);
  not not_1 (not_1_out, K);
  and and_2 (and_2_out, not_1_out, Q);
  or or_1 (or_1_out, and_1_out, and_2_out);
  Clock clock_1 (.out(clock_1_out));
  nand nand_1 (nand_1_out, or_1_out, clock_1_out);
  not nand_2 (nand_2_out, nand_1_out);  // NAND_Gate
  not not_2 (not_2_out, clock_1_out);
  nand nand_3 (nand_3_out, nand_1_out, nand_4_out);
  nand nand_4 (nand_4_out, nand_3_out, nand_2_out);
  nand nand_5 (nand_5_out, nand_3_out, not_2_out);
  nand nand_6 (nand_6_out, not_2_out, nand_4_out);
  nand nand_7 (Q, nand_5_out, Q_prime);
  nand nand_8 (Q_prime, Q, nand_6_out);

  // Notes on the sheet:
  //   D
  //   n
  //   n
endmodule
