// Logisim project adder with two 4x1 multiplexers.circ as structural Verilog: 1 circuit, main circuit main
module main (
  input  Z,
  input  X,
  input  Y,
  output S,
  output C
);

  wire and_1_out, and_2_out, and_3_out, and_4_out, and_5_out, and_6_out, and_7_out, and_8_out, not_1_out,
       not_2_out, not_4_out;

  not not_1 (not_1_out, Z);
  not not_2 (not_2_out, X);
  not not_3 (not_2_out, X);
  not not_4 (not_4_out, Y);
  not not_5 (not_2_out, X);
  not not_6 (not_4_out, Y);
  and and_1 (and_1_out, Z, not_2_out, not_4_out);
  and and_2 (and_2_out, not_1_out, not_2_out, Y);
  and and_3 (and_3_out, not_1_out, X, not_4_out);
  and and_4 (and_4_out, Z, X, Y);
  not not_7 (not_4_out, Y);
  and and_5 (and_5_out, 1'b0, not_2_out, not_4_out);
  and and_6 (and_6_out, Z, not_2_out, Y);
  and and_7 (and_7_out, Z, X, not_4_out);
  and and_8 (and_8_out, 1'b1, X, Y);
  or or_1 (S, and_1_out, and_2_out, and_3_out, and_4_out);
  or or_2 (C, and_5_out, and_6_out, and_7_out, and_8_out);
endmodule
